# Fritzing sketch midi_out (saved by Fritzing 0.9.9b)
breadboards: 1

parts:
  R1 = Resistor [tolerance=±5% resistance=68 package="1206 [SMD]"]
  U2 = MIDI_CONN_FEMALE [package=din_5_female]
  Mod1 = Raspberry Pi Pico
  R6 = Resistor [tolerance=±5% resistance=68 package="1206 [SMD]"]

nets:
  N1: R1.Pin_0, U2.MIDI_IN
  N2: R1.Pin_1, Mod1.pin_3, Mod1.pin_8, Mod1.pin_13, Mod1.pin_18, Mod1.pin_23, Mod1.pin_28, Mod1.pin_33, Mod1.pin_38, Mod1.pin_42
  N3: U2.MIDI_OUT, R6.Pin_0
  3.3V: Mod1.pin_36, R6.Pin_1

custom parts:
  Raspberry Pi Pico: Raspberry Pi Pico. Based around the RP2040 microcontroller the Pico is a low cost microcontroller device bringing Raspberry Pi quality, cost, and easy of use to the microcontroller space. Jan 2021, Split part in to two versions: tht (this one) and SMD. This one will drill holes for a .1 in header in pcb to allow plugging in the module as well as providing pads to solder the module to the top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
