# Fritzing sketch midilib (saved by Fritzing 0.9.9b)
breadboards: 1

parts:
  R1 = Resistor [tolerance=±5% resistance=68 package="1206 [SMD]"]
  R2 = Resistor [tolerance=±5% resistance=220 package="1206 [SMD]"]
  U1 = OPTO_DARL_6N138S [package=8-smd]
  U2 = MIDI_CONN_FEMALE [package=din_5_female]
  U3 = MIDI_CONN_FEMALE [package=din_5_female]
  D1 = Diode [package=diode-1n4148]
  R4 = Resistor [tolerance=±5% resistance=1k package="2010 [SMD]"]
  R5 = Resistor [tolerance=±5% resistance=270 package="2010 [SMD]"]
  Mod1 = Raspberry Pi Pico
  R6 = Resistor [tolerance=±5% resistance=68 package="1206 [SMD]"]

nets:
  N1: R1.Pin_0, U2.MIDI_IN
  N2: R1.Pin_1, U1.GND, R4.Pin_0, Mod1.pin_3, Mod1.pin_8, Mod1.pin_13, Mod1.pin_18, Mod1.pin_23, Mod1.pin_28, Mod1.pin_33, Mod1.pin_38, Mod1.pin_42
  N3: R2.Pin_0, U3.MIDI_OUT
  N4: R2.Pin_1, U1.A, D1.C
  N5: U1.C, U3.MIDI_IN
  N6: U1.VOUT, R5.Pin_1, Mod1.pin_9
  N7: U1.VCC, R5.Pin_0, Mod1.pin_36, R6.Pin_0
  N8: U2.MIDI_OUT, R6.Pin_1

custom parts:
  Raspberry Pi Pico: Raspberry Pi Pico. Based around the RP2040 microcontroller the Pico is a low cost microcontroller device bringing Raspberry Pi quality, cost, and easy of use to the microcontroller space. Jan 2021, Split part in to two versions: tht (this one) and SMD. This one will drill holes for a .1 in header in pcb to allow plugging in the module as well as providing pads to solder the module to the top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
